// Logisim project final.circ as structural Verilog: 10 circuits, main circuit main
module main (
  input  enable
);

  wire and_1_out, clock_1_out, hour_1_a, hour_1_a_2, hour_1_g, hour_1_g_2, hour_1_out, hour_1_out_4,
       hour_1_out_5, hour_1_out_6, hour_1_out_7, hour_1_out_8, hour_1_out_11, hour_1_out_12, hour_1_out_13,
       hour_1_out_14, hour_1_out_15, j_k_ff_1_qn, min_1_a3, min_1_a4, min_1_g3, min_1_g4, min_1_out,
       min_1_out_3, min_1_out_4, min_1_out_5, min_1_out_8, min_1_out_9, min_1_out_10, min_1_out_11,
       min_1_out_12, min_1_out_15, min_1_out_16, seconds_1_a1, seconds_1_a2, seconds_1_g1, seconds_1_g2,
       seconds_1_out, seconds_1_out_4, seconds_1_out_5, seconds_1_out_6, seconds_1_out_7, seconds_1_out_8,
       seconds_1_out_11, seconds_1_out_12, seconds_1_out_13, seconds_1_out_14, seconds_1_out_15;
  wire [7:0] undriven;
  wire [8:0] undriven_2, undriven_3, undriven_4;

  _7_Segment_Display u_7_segment_display_1 (
    .g(1'b1), .f(1'b1), .a(1'b1), .b(1'b1), .e(1'b1), .c(j_k_ff_1_qn));  // open: d, dp
  DotMatrix #(.matrixcols(9), .matrixrows(9)) dotmatrix_1 (
    .col0({9{1'b1}}), .col1({1'b1, undriven}), .col2({undriven_2[8], 1'b1, undriven_2[6:0]}),
    .col3({undriven_3[8:7], 1'b1, undriven_3[5:0]}), .col4({undriven_4[8:6], 1'b1, undriven_4[4:0]}),
    .col5({undriven_3[8:7], 1'b1, undriven_3[5:0]}), .col6({undriven_2[8], 1'b1, undriven_2[6:0]}),
    .col7({1'b1, undriven}), .col8({9{1'b1}}));
  J_K_Flip_Flop j_k_ff_1 (
    .J(and_1_out), .clk(clock_1_out), .K(and_1_out), .Qn(j_k_ff_1_qn));  // open: Q, preset, en, reset
  and and_1 (and_1_out, hour_1_out, min_1_out, seconds_1_out);
  _7_Segment_Display u_7_segment_display_2 (
    .g(hour_1_g), .f(hour_1_out_8), .a(hour_1_a), .b(hour_1_out_4), .e(hour_1_out_7), .d(hour_1_out_6),
    .c(hour_1_out_5));  // open: dp
  _7_Segment_Display u_7_segment_display_3 (
    .g(hour_1_g_2), .f(hour_1_out_15), .a(hour_1_a_2), .b(hour_1_out_11), .e(hour_1_out_14),
    .d(hour_1_out_13), .c(hour_1_out_12));  // open: dp
  hour hour_1 (
    .out(hour_1_out), .a(hour_1_a), .out_4(hour_1_out_4), .out_5(hour_1_out_5), .out_6(hour_1_out_6),
    .out_7(hour_1_out_7), .out_8(hour_1_out_8), .g(hour_1_g), .a_2(hour_1_a_2), .out_11(hour_1_out_11),
    .out_12(hour_1_out_12), .out_13(hour_1_out_13), .out_14(hour_1_out_14), .out_15(hour_1_out_15),
    .g_2(hour_1_g_2), .\input (min_1_out), .clock(clock_1_out));
  _7_Segment_Display u_7_segment_display_4 (
    .g(min_1_g4), .f(min_1_out_5), .a(min_1_a4), .b(min_1_out_15), .e(min_1_out_4), .d(min_1_out_3),
    .c(min_1_out_16));  // open: dp
  _7_Segment_Display u_7_segment_display_5 (
    .g(min_1_g3), .f(min_1_out_12), .a(min_1_a3), .b(min_1_out_8), .e(min_1_out_11), .d(min_1_out_10),
    .c(min_1_out_9));  // open: dp
  min min_1 (
    .out(min_1_out), .a4(min_1_a4), .out_15(min_1_out_15), .out_16(min_1_out_16), .out_3(min_1_out_3),
    .out_4(min_1_out_4), .out_5(min_1_out_5), .g4(min_1_g4), .a3(min_1_a3), .out_8(min_1_out_8),
    .out_9(min_1_out_9), .out_10(min_1_out_10), .out_11(min_1_out_11), .out_12(min_1_out_12), .g3(min_1_g3),
    .\input (seconds_1_out), .clock(clock_1_out));
  _7_Segment_Display u_7_segment_display_6 (
    .g(seconds_1_g1), .f(seconds_1_out_8), .a(seconds_1_a1), .b(seconds_1_out_4), .e(seconds_1_out_7),
    .d(seconds_1_out_6), .c(seconds_1_out_5));  // open: dp
  _7_Segment_Display u_7_segment_display_7 (
    .g(seconds_1_g2), .f(seconds_1_out_15), .a(seconds_1_a2), .b(seconds_1_out_11), .e(seconds_1_out_14),
    .d(seconds_1_out_13), .c(seconds_1_out_12));  // open: dp
  seconds seconds_1 (
    .out(seconds_1_out), .a2(seconds_1_a2), .out_11(seconds_1_out_11), .out_12(seconds_1_out_12),
    .out_13(seconds_1_out_13), .out_14(seconds_1_out_14), .out_15(seconds_1_out_15), .g2(seconds_1_g2),
    .a1(seconds_1_a1), .out_4(seconds_1_out_4), .out_5(seconds_1_out_5), .out_6(seconds_1_out_6),
    .out_7(seconds_1_out_7), .out_8(seconds_1_out_8), .g1(seconds_1_g1), .clock(clock_1_out), .enable(enable));
  Clock clock_1 (.out(clock_1_out));

  // Notes on the sheet:
  //   hours
  //   minutes
  //   secondes
endmodule

module _0_to_9_counter (
  input  \input ,
  input  clock,
  output out,
  output x1,
  output x2,
  output x3,
  output x4
);

  wire and_1_out, and_2_out, and_3_out, and_4_out;

  and and_1 (and_1_out, \input , x4);
  and and_2 (and_2_out, and_1_out, x3);
  and and_3 (and_3_out, and_2_out, x2);
  and and_4 (and_4_out, x3, x1);
  J_K_Flip_Flop j_k_ff_1 (.J(\input ), .clk(clock), .K(\input ), .Q(x4), .reset(and_4_out));  // open: Qn, preset, en
  J_K_Flip_Flop j_k_ff_2 (
    .J(and_1_out), .clk(clock), .K(and_1_out), .Q(x3), .reset(and_4_out));  // open: Qn, preset, en
  J_K_Flip_Flop j_k_ff_3 (
    .J(and_2_out), .clk(clock), .K(and_2_out), .Q(x2), .reset(and_4_out));  // open: Qn, preset, en
  J_K_Flip_Flop j_k_ff_4 (
    .J(and_3_out), .clk(clock), .K(and_3_out), .Q(x1), .reset(and_4_out));  // open: Qn, preset, en
  and and_5 (out, x4, \input , x1);

  // Notes on the sheet:
  //   0 to 9 counter
endmodule

module _0_to_5_counter (
  input  \input ,
  input  clock,
  output \output ,
  output m1,
  output m2,
  output m3
);

  wire and_1_out, and_2_out, and_3_out, and_5_out;

  and and_1 (and_1_out, \input , m3);
  and and_2 (and_2_out, and_1_out, m2);
  and and_3 (and_3_out, m2, m1);
  J_K_Flip_Flop j_k_ff_1 (.J(\input ), .clk(clock), .K(\input ), .Q(m3), .reset(and_3_out));  // open: Qn, preset, en
  J_K_Flip_Flop j_k_ff_2 (
    .J(and_1_out), .clk(clock), .K(and_1_out), .Q(m2), .reset(and_3_out));  // open: Qn, preset, en
  J_K_Flip_Flop j_k_ff_3 (
    .J(and_2_out), .clk(clock), .K(and_2_out), .Q(m1), .reset(and_3_out));  // open: Qn, preset, en
  and and_4 (\output , \input , and_5_out);
  and and_5 (and_5_out, m3, m1);

  // Notes on the sheet:
  //   0 to 5 counter
endmodule

module _7_segment_1 (
  input  x1,
  input  x2,
  input  x3,
  input  x4,
  output a,
  output b,
  output c,
  output d,
  output e,
  output f,
  output g
);

  wire and_1_out, and_2_out, and_3_out, and_4_out, and_5_out, and_6_out, and_7_out, and_8_out, and_9_out,
       and_10_out, and_11_out, and_12_out, and_13_out, and_14_out, and_15_out, and_16_out, and_17_out,
       and_18_out, not_1_out, not_2_out, not_3_out, not_4_out, not_5_out, not_6_out, not_7_out, not_8_out,
       not_9_out, not_10_out, not_11_out, not_12_out, not_13_out, not_14_out, not_15_out, not_16_out,
       not_17_out, not_18_out, not_19_out, not_20_out, not_21_out, or_1_out, or_2_out, or_3_out, or_4_out,
       or_5_out, or_7_out, or_8_out, or_9_out, or_10_out, or_11_out, or_12_out, or_15_out, or_16_out;

  not not_1 (not_1_out, x2);
  and and_1 (and_1_out, not_1_out, not_2_out);
  not not_2 (not_2_out, x4);
  and and_2 (and_2_out, x2, x4);
  not not_3 (not_3_out, x2);
  not not_4 (not_4_out, x3);
  and and_3 (and_3_out, not_4_out, not_5_out);
  not not_5 (not_5_out, x4);
  not not_6 (not_6_out, x3);
  or or_1 (or_1_out, not_6_out, x4);
  or or_2 (or_2_out, x2, x1);
  not not_7 (not_7_out, x2);
  and and_4 (and_4_out, not_7_out, not_8_out);
  not not_8 (not_8_out, x4);
  not not_9 (not_9_out, x2);
  and and_5 (and_5_out, not_9_out, x3);
  not not_10 (not_10_out, x4);
  and and_6 (and_6_out, x2, not_11_out);
  not not_11 (not_11_out, x3);
  not not_12 (not_12_out, x2);
  and and_7 (and_7_out, not_12_out, not_13_out);
  not not_13 (not_13_out, x4);
  and and_8 (and_8_out, x3, not_14_out);
  not not_14 (not_14_out, x4);
  not not_15 (not_15_out, x3);
  and and_9 (and_9_out, not_15_out, not_16_out);
  not not_16 (not_16_out, x4);
  and and_10 (and_10_out, x2, not_17_out);
  not not_17 (not_17_out, x3);
  and and_11 (and_11_out, x2, not_18_out);
  not not_18 (not_18_out, x4);
  not not_19 (not_19_out, x2);
  and and_12 (and_12_out, not_19_out, x3);
  and and_13 (and_13_out, x2, not_20_out);
  not not_20 (not_20_out, x3);
  and and_14 (and_14_out, x2, not_21_out);
  not not_21 (not_21_out, x4);
  or or_3 (or_3_out, and_1_out, x3);
  or or_4 (or_4_out, and_2_out, x1);
  or or_5 (or_5_out, not_3_out, and_3_out);
  and and_15 (and_15_out, x3, x4);
  or or_6 (c, or_1_out, or_2_out);
  or or_7 (or_7_out, and_4_out, and_5_out);
  and and_16 (and_16_out, x3, not_10_out);
  and and_17 (and_17_out, and_6_out, x4);
  or or_8 (or_8_out, and_7_out, and_8_out);
  and and_18 (and_18_out, x1, x3);
  or or_9 (or_9_out, and_9_out, and_10_out);
  or or_10 (or_10_out, and_11_out, x1);
  or or_11 (or_11_out, and_12_out, and_13_out);
  or or_12 (or_12_out, and_14_out, x1);
  or or_13 (a, or_3_out, or_4_out);
  or or_14 (b, or_5_out, and_15_out);
  or or_15 (or_15_out, or_7_out, and_16_out);
  or or_16 (or_16_out, and_17_out, x1);
  or or_17 (e, or_8_out, and_18_out);
  or or_18 (f, or_9_out, or_10_out);
  or or_19 (g, or_11_out, or_12_out);
  or or_20 (d, or_15_out, or_16_out);

  // Notes on the sheet:
  //   7 segment with 4 inputs
endmodule

module _7_segment_2 (
  input  x1,
  input  x2,
  input  x3,
  output a,
  output b,
  output c,
  output d,
  output e,
  output f,
  output g
);

  wire and_1_out, and_2_out, and_3_out, and_4_out, and_6_out, not_1_out, not_2_out, not_3_out, not_4_out,
       not_5_out, not_6_out, not_7_out, not_8_out, not_9_out, not_10_out, not_11_out;

  not not_1 (not_1_out, x1);
  not not_2 (not_2_out, x3);
  not not_3 (not_3_out, x1);
  not not_4 (not_4_out, x3);
  not not_5 (not_5_out, x2);
  not not_6 (not_6_out, x1);
  not not_7 (not_7_out, x3);
  not not_8 (not_8_out, x1);
  not not_9 (not_9_out, x3);
  not not_10 (not_10_out, x2);
  not not_11 (not_11_out, x3);
  or or_1 (g, x2, x1);
  and and_1 (and_1_out, not_1_out, not_2_out);
  and and_2 (and_2_out, x1, x3);
  or or_2 (b, not_3_out, not_4_out);
  or or_3 (c, not_5_out, x3);
  and and_3 (and_3_out, not_6_out, not_7_out);
  and and_4 (and_4_out, x1, x3);
  and and_5 (e, not_8_out, not_9_out);
  and and_6 (and_6_out, not_10_out, not_11_out);
  or or_4 (a, and_1_out, x2, and_2_out);
  or or_5 (d, and_3_out, x2, and_4_out);
  or or_6 (f, and_6_out, x1);

  // Notes on the sheet:
  //   7 segment with 3 inputs
endmodule

module seconds (
  input  clock,
  input  enable,
  output a1,
  output out_4,
  output out_5,
  output out_6,
  output out_7,
  output out_8,
  output g1,
  output a2,
  output out_11,
  output out_12,
  output out_13,
  output out_14,
  output out_15,
  output g2,
  output out
);

  wire n0_to_5_counter_1_m1, n0_to_5_counter_1_m2, n0_to_5_counter_1_m3, n0_to_9_counter_1_out,
       n0_to_9_counter_1_x1, n0_to_9_counter_1_x2, n0_to_9_counter_1_x3, n0_to_9_counter_1_x4;

  _7_segment_2 u_7_segment_2_1 (
    .x1(n0_to_5_counter_1_m1), .x2(n0_to_5_counter_1_m2), .x3(n0_to_5_counter_1_m3), .a(a2), .b(out_11),
    .c(out_12), .d(out_13), .e(out_14), .f(out_15), .g(g2));
  _0_to_5_counter u_0_to_5_counter_1 (
    .\input (n0_to_9_counter_1_out), .clock(clock), .\output (out), .m1(n0_to_5_counter_1_m1),
    .m2(n0_to_5_counter_1_m2), .m3(n0_to_5_counter_1_m3));
  _7_segment_1 u_7_segment_1_1 (
    .x1(n0_to_9_counter_1_x1), .x2(n0_to_9_counter_1_x2), .x3(n0_to_9_counter_1_x3),
    .x4(n0_to_9_counter_1_x4), .a(a1), .b(out_4), .c(out_5), .d(out_6), .e(out_7), .f(out_8), .g(g1));
  _0_to_9_counter u_0_to_9_counter_1 (
    .\input (enable), .clock(clock), .out(n0_to_9_counter_1_out), .x1(n0_to_9_counter_1_x1),
    .x2(n0_to_9_counter_1_x2), .x3(n0_to_9_counter_1_x3), .x4(n0_to_9_counter_1_x4));
endmodule

module min (
  input  \input ,
  input  clock,
  output out_3,
  output out_4,
  output out_5,
  output g4,
  output a3,
  output out_8,
  output out_9,
  output out_10,
  output out_11,
  output out_12,
  output g3,
  output a4,
  output out_15,
  output out_16,
  output out
);

  wire n0_to_5_counter_1_m1, n0_to_5_counter_1_m2, n0_to_5_counter_1_m3, n0_to_9_counter_1_out,
       n0_to_9_counter_1_x1, n0_to_9_counter_1_x2, n0_to_9_counter_1_x3, n0_to_9_counter_1_x4;

  _7_segment_2 u_7_segment_2_1 (
    .x1(n0_to_5_counter_1_m1), .x2(n0_to_5_counter_1_m2), .x3(n0_to_5_counter_1_m3), .a(a4), .b(out_15),
    .c(out_16), .d(out_3), .e(out_4), .f(out_5), .g(g4));
  _0_to_5_counter u_0_to_5_counter_1 (
    .\input (n0_to_9_counter_1_out), .clock(clock), .\output (out), .m1(n0_to_5_counter_1_m1),
    .m2(n0_to_5_counter_1_m2), .m3(n0_to_5_counter_1_m3));
  _7_segment_1 u_7_segment_1_1 (
    .x1(n0_to_9_counter_1_x1), .x2(n0_to_9_counter_1_x2), .x3(n0_to_9_counter_1_x3),
    .x4(n0_to_9_counter_1_x4), .a(a3), .b(out_8), .c(out_9), .d(out_10), .e(out_11), .f(out_12), .g(g3));
  _0_to_9_counter u_0_to_9_counter_1 (
    .\input (\input ), .clock(clock), .out(n0_to_9_counter_1_out), .x1(n0_to_9_counter_1_x1),
    .x2(n0_to_9_counter_1_x2), .x3(n0_to_9_counter_1_x3), .x4(n0_to_9_counter_1_x4));
endmodule

module hour (
  input  \input ,
  input  clock,
  output a,
  output out_4,
  output out_5,
  output out_6,
  output out_7,
  output out_8,
  output g,
  output a_2,
  output out_11,
  output out_12,
  output out_13,
  output out_14,
  output out_15,
  output g_2,
  output out
);

  wire n0_to_12_counter_1_x1, n0_to_12_counter_1_x2, n0_to_12_counter_1_x3, n0_to_12_counter_1_x4,
       n0_to_12_counter_1_y1, n0_to_12_counter_1_y2;

  and and_1 (out, n0_to_12_counter_1_x2, n0_to_12_counter_1_y2);
  _7_segment_3 u_7_segment_3_1 (
    .a(n0_to_12_counter_1_y1), .a_2(a), .b(out_4), .c(out_5), .d(out_6), .e(out_7), .f(out_8), .g(g));
  _0_to_12_counter u_0_to_12_counter_1 (
    .\input (\input ), .clock(clock), .y2(n0_to_12_counter_1_y2), .y1(n0_to_12_counter_1_y1),
    .x1(n0_to_12_counter_1_x1), .x2(n0_to_12_counter_1_x2), .x3(n0_to_12_counter_1_x3),
    .x4(n0_to_12_counter_1_x4));
  _7_segment_1 u_7_segment_1_1 (
    .x1(n0_to_12_counter_1_x4), .x2(n0_to_12_counter_1_x3), .x3(n0_to_12_counter_1_x2),
    .x4(n0_to_12_counter_1_x1), .a(a_2), .b(out_11), .c(out_12), .d(out_13), .e(out_14), .f(out_15), .g(g_2));
endmodule

module _0_to_12_counter (
  input  \input ,
  input  clock,
  output y2,
  output y1,
  output x1,
  output x2,
  output x3,
  output x4
);

  wire and_1_out, and_2_out, and_3_out, and_4_out, and_5_out, and_6_out, and_7_out, or_1_out;

  and and_1 (and_1_out, \input , x1);
  and and_2 (and_2_out, and_1_out, x2);
  and and_3 (and_3_out, and_2_out, x3);
  and and_4 (and_4_out, x2, x4);
  and and_5 (and_5_out, y2, x1, x2);
  J_K_Flip_Flop j_k_ff_1 (.J(\input ), .clk(clock), .K(\input ), .Q(x1));  // open: Qn, preset, en, reset
  J_K_Flip_Flop j_k_ff_2 (.J(and_1_out), .clk(clock), .K(and_1_out), .Q(x2), .reset(or_1_out));  // open: Qn, preset, en
  J_K_Flip_Flop j_k_ff_3 (.J(and_2_out), .clk(clock), .K(and_2_out), .Q(x3), .reset(or_1_out));  // open: Qn, preset, en
  J_K_Flip_Flop j_k_ff_4 (.J(and_3_out), .clk(clock), .K(and_3_out), .Q(x4), .reset(or_1_out));  // open: Qn, preset, en
  or or_1 (or_1_out, and_4_out, and_5_out);
  and and_6 (and_6_out, x1, \input , x4);
  J_K_Flip_Flop j_k_ff_5 (
    .J(and_6_out), .clk(clock), .K(and_6_out), .Q(y2), .Qn(y1), .reset(and_7_out));  // open: preset, en
  and and_7 (and_7_out, x1, x2, y2);

  // Notes on the sheet:
  //   0 to 12 counter
endmodule

module _7_segment_3 (
  input  a,
  output a_2,
  output b,
  output c,
  output d,
  output e,
  output f,
  output g
);


  assign a_2 = a;
  assign b = 1'b1;
  assign c = 1'b1;
  assign d = a;
  assign e = a;
  assign f = a;
  assign g = 1'b0;
endmodule
